# Fritzing sketch relay_buttons3_nodemcu (saved by Fritzing 0.9.3b)

parts:
  Part1 = KY-004 Key Switch Module [package="Breakout board"]
  Part2 = KY-004 Key Switch Module [package="Breakout board"]
  COMPUTER_FAN1 = Computer fan
  Componente1 = NodeMcu base board
  L1 = LED Light Transformer [package=THT]
  L2 = LED Light [package=THT]
  Componente2 = Keyes Double Relay [package=THT]
  AC_PLUG1 = AC Plug
  Part3 = KY-004 Key Switch Module [package="Breakout board"]

nets:
  N1: Part1.S, Componente1.D5
  VIN: Part1.Vin, Part2.Vin, Componente1.3V, Part3.Vin
  N2: Part1.-, Part2.-, Componente1.GND#44, Componente1.GND#46, Componente1.GND#48, Part3.-
  N3: Part2.S, Componente1.D6
  N4: COMPUTER_FAN1.BLACK, Componente1.G, Componente1.GND#16, Componente1.GND#52, Componente1.GND#58, Componente2.GND
  N5: Componente1.D7, Part3.S
  N6: Componente1.VU, Componente1.VUSB, Componente2.VCC
  N7: Componente1.D1, Componente2.IN1
  N8: Componente1.D2, Componente2.IN2
  N9: L1.N, AC_PLUG1.BLACK
  N10: L1.-, L2.-
  N11: L1.+, L2.+

custom parts:
  KY-004 Key Switch Module: Arduino Key Switch Module Keyes KY-004 is a push button that will output a high signal when pressed.
  Computer fan: This is a 5V computer fan
  NodeMcu base board: ESP8266 WiFi Expansion Board For NodeMCU ESP-12E
  Keyes Double Relay: The Keyes 5V double relay module is suitable for SCM development, home appliance control. It uses a 5V~12V TIL control signal which can control DC / AC signal.
  AC Plug: This is a 220V/110 Vac plug
