# Fritzing sketch relay_buttons3_wemosD1R32 (saved by Fritzing 0.9.3b)

parts:
  Part1 = KY-004 Key Switch Module [package="Breakout board"]
  Part2 = KY-004 Key Switch Module [package="Breakout board"]
  COMPUTER_FAN1 = Computer fan
  WeMos_D1_R32_Shield1 = WeMos D1 R32 with Arduino Sensor Shield v5
  L1 = LED Light [package=THT]
  L2 = LED Light Transformer [package=THT]
  Componente1 = Keyes Double Relay [package=THT]
  Part3 = KY-004 Key Switch Module [package="Breakout board"]
  AC_PLUG1 = AC Plug

nets:
  N1: Part1.S, WeMos_D1_R32_Shield1.D2
  N2: Part1.Vin, WeMos_D1_R32_Shield1.5V#45
  N3: Part1.-, WeMos_D1_R32_Shield1.GND#22
  N4: Part2.S, WeMos_D1_R32_Shield1.GND#23
  N5: Part2.Vin, WeMos_D1_R32_Shield1.5V#46
  N6: Part2.-, WeMos_D1_R32_Shield1.D3
  N7: COMPUTER_FAN1.BLACK, WeMos_D1_R32_Shield1.GND#42
  N8: WeMos_D1_R32_Shield1.D4, Part3.S
  N9: WeMos_D1_R32_Shield1.D5, Componente1.IN2
  N10: WeMos_D1_R32_Shield1.D6, Componente1.IN1
  N11: WeMos_D1_R32_Shield1.GND#24, Part3.-
  N12: WeMos_D1_R32_Shield1.GND#27, Componente1.GND
  N13: WeMos_D1_R32_Shield1.5V#47, Part3.Vin
  N14: WeMos_D1_R32_Shield1.5V#49, Componente1.VCC
  N15: L1.-, L2.-
  N16: L1.+, L2.+
  N17: L2.N, AC_PLUG1.BLACK

custom parts:
  KY-004 Key Switch Module: Arduino Key Switch Module Keyes KY-004 is a push button that will output a high signal when pressed.
  Computer fan: This is a 5V computer fan
  WeMos D1 R32 with Arduino Sensor Shield v5: The D1 R32 is a mini wifi board based on the ESP32 with an Arduino Sensor Shield v5
  Keyes Double Relay: The Keyes 5V double relay module is suitable for SCM development, home appliance control. It uses a 5V~12V TIL control signal which can control DC / AC signal.
  AC Plug: This is a 220V/110 Vac plug
