# Fritzing sketch relay_buttons_leonardo (saved by Fritzing 0.9.3b)

parts:
  KY-1 = Keyes Relay [package=THT]
  Part1 = KY-004 Key Switch Module [package="Breakout board"]
  Part2 = KY-004 Key Switch Module [package="Breakout board"]
  COMPUTER_FAN1 = Computer fan
  Leonardo_Shield1 = Arduino Leonardo with Arduino Sensor Shield v5

nets:
  N1: KY-1.signal, Leonardo_Shield1.D7, Leonardo_Shield1.5V#47
  N2: KY-1.power, Leonardo_Shield1.5V#50
  N3: KY-1.ground, Leonardo_Shield1.GND#28
  N4: KY-1.NC, COMPUTER_FAN1.RED
  N5: KY-1.C, Leonardo_Shield1.5V#58
  N6: Part1.S, Part1.Vin, Leonardo_Shield1.5V#45
  N7: Part1.-, Leonardo_Shield1.GND#22
  N8: Part2.S, Leonardo_Shield1.GND#23
  N9: Part2.Vin, Leonardo_Shield1.5V#46
  N10: Part2.-, Leonardo_Shield1.D3, Leonardo_Shield1.GND#79
  N11: COMPUTER_FAN1.BLACK, Leonardo_Shield1.GND#42

custom parts:
  Keyes Relay: The Keyes 5V relay module is suitable for SCM development, home appliance control. It uses a 5V~12V TIL control signal which can control DC / AC signal.
  KY-004 Key Switch Module: Arduino Key Switch Module Keyes KY-004 is a push button that will output a high signal when pressed.
  Computer fan: This is a 5V computer fan
  Arduino Leonardo with Arduino Sensor Shield v5: The D1 R32 is a mini wifi board based on the ESP32 with an Arduino Sensor Shield v5
