# Fritzing sketch relay_buttons_nodemcu (saved by Fritzing 0.9.3b)

parts:
  KY-1 = Keyes Relay [package=THT]
  Part1 = KY-004 Key Switch Module [package="Breakout board"]
  Part2 = KY-004 Key Switch Module [package="Breakout board"]
  COMPUTER_FAN1 = Computer fan
  Componente1 = NodeMcu base board

nets:
  N1: KY-1.signal, Componente1.D2
  N2: KY-1.power, KY-1.C, Componente1.VU, Componente1.VUSB
  N3: KY-1.ground, COMPUTER_FAN1.BLACK, Componente1.G, Componente1.GND#16, Componente1.GND#52, Componente1.GND#58
  N4: KY-1.NC, COMPUTER_FAN1.RED
  N5: Part1.S, Componente1.D5
  VIN: Part1.Vin, Part2.Vin, Componente1.3V
  N6: Part1.-, Part2.-, Componente1.GND#44, Componente1.GND#46
  N7: Part2.S, Componente1.D6

custom parts:
  Keyes Relay: The Keyes 5V relay module is suitable for SCM development, home appliance control. It uses a 5V~12V TIL control signal which can control DC / AC signal.
  KY-004 Key Switch Module: Arduino Key Switch Module Keyes KY-004 is a push button that will output a high signal when pressed.
  Computer fan: This is a 5V computer fan
  NodeMcu base board: ESP8266 WiFi Expansion Board For NodeMCU ESP-12E
