# Fritzing sketch relay_buttons_wemosD1R32 (saved by Fritzing 0.9.3b)

parts:
  KY-1 = Keyes Relay [package=THT]
  Part1 = KY-004 Key Switch Module [package="Breakout board"]
  Part2 = KY-004 Key Switch Module [package="Breakout board"]
  COMPUTER_FAN1 = Computer fan
  WeMos_D1_R32_Shield1 = WeMos D1 R32 with Arduino Sensor Shield v5

nets:
  N1: KY-1.signal, WeMos_D1_R32_Shield1.D7
  N2: KY-1.power, WeMos_D1_R32_Shield1.5V#50
  N3: KY-1.ground, WeMos_D1_R32_Shield1.GND#28
  N4: KY-1.NC, COMPUTER_FAN1.RED
  N5: KY-1.C, WeMos_D1_R32_Shield1.5V#58
  N6: Part1.S, WeMos_D1_R32_Shield1.D2
  N7: Part1.Vin, WeMos_D1_R32_Shield1.5V#45
  N8: Part1.-, WeMos_D1_R32_Shield1.GND#22
  N9: Part2.S, WeMos_D1_R32_Shield1.GND#23
  N10: Part2.Vin, WeMos_D1_R32_Shield1.5V#46
  N11: Part2.-, WeMos_D1_R32_Shield1.D3
  N12: COMPUTER_FAN1.BLACK, WeMos_D1_R32_Shield1.GND#42

custom parts:
  Keyes Relay: The Keyes 5V relay module is suitable for SCM development, home appliance control. It uses a 5V~12V TIL control signal which can control DC / AC signal.
  KY-004 Key Switch Module: Arduino Key Switch Module Keyes KY-004 is a push button that will output a high signal when pressed.
  Computer fan: This is a 5V computer fan
  WeMos D1 R32 with Arduino Sensor Shield v5: The D1 R32 is a mini wifi board based on the ESP32 with an Arduino Sensor Shield v5
