# Fritzing sketch switch_leonardo (saved by Fritzing 0.9.3b)

parts:
  Part1 = KY-004 Key Switch Module [package="Breakout board"]
  Leonardo_Shield2 = Arduino Leonardo with Arduino Sensor Shield v5

nets:
  N1: Part1.S, Leonardo_Shield2.D2
  VIN: Part1.Vin, Leonardo_Shield2.5V
  N2: Part1.-, Leonardo_Shield2.GND

custom parts:
  KY-004 Key Switch Module: Arduino Key Switch Module Keyes KY-004 is a push button that will output a high signal when pressed.
  Arduino Leonardo with Arduino Sensor Shield v5: The D1 R32 is a mini wifi board based on the ESP32 with an Arduino Sensor Shield v5
