# Fritzing sketch switch_nano (saved by Fritzing 0.9.3b)

parts:
  Componente1 = Arduino Nano (Rev3.0)
  Part1 = KY-004 Key Switch Module [package="Breakout board"]

nets:
  N1: Componente1.D2, Part1.S
  N2: Componente1.GND, Part1.-
  5V: Componente1.5V, Part1.Vin

custom parts:
  Arduino Nano (Rev3.0): Arduino Nano 3.0 IO expansion board
  KY-004 Key Switch Module: Arduino Key Switch Module Keyes KY-004 is a push button that will output a high signal when pressed.
