# Fritzing sketch switch_nodemcu (saved by Fritzing 0.9.3b)

parts:
  Part1 = KY-004 Key Switch Module [package="Breakout board"]
  Componente1 = NodeMcu base board

nets:
  N1: Part1.S, Componente1.D2
  VIN: Part1.Vin, Componente1.3V3, Componente1.3V
  N2: Part1.-, Componente1.G, Componente1.GND

custom parts:
  KY-004 Key Switch Module: Arduino Key Switch Module Keyes KY-004 is a push button that will output a high signal when pressed.
  NodeMcu base board: ESP8266 WiFi Expansion Board For NodeMCU ESP-12E
